# Fritzing sketch circuit (saved by Fritzing 0.8.6b)
breadboards: 1

parts:
  Raspberry_Pi_A1 = Raspberry Pi A
  R1 = Resistor [tolerance=±5% resistance=10k package=THT]
  S1 = Round Pushbutton  # not connected
  S2 = Round Pushbutton  # not connected
  S3 = Round Pushbutton  # not connected
  R2 = Resistor [tolerance=±5% resistance=10k package=THT]
  R3 = Resistor [tolerance=±5% resistance=10k package=THT]
  LED1 = LED - 5mm [color="Red (633nm)" package="5 mm [THT]"]  # not connected
  LED2 = LED - 5mm [color="Red (633nm)" package="5 mm [THT]"]  # not connected
  LED3 = LED - 5mm [color="Red (633nm)" package="5 mm [THT]"]  # not connected
  S4 = SPST Switch [package=r_sw_th]  # not connected

nets:
  3V3: Raspberry_Pi_A1.3V3, Raspberry_Pi_A1.5V
  N1: Raspberry_Pi_A1.GND, R1.Pin_1, R2.Pin_1, R3.Pin_1
  N2: Raspberry_Pi_A1.GPIO_14, R1.Pin_0
  N3: Raspberry_Pi_A1.GPIO_18, R2.Pin_0
  N4: Raspberry_Pi_A1.GPIO_24, R3.Pin_0
